# Fritzing sketch pc_transciever (saved by Fritzing 0.9.2b)

parts:
  RFM1 = RFM69HCW ISM Transciever
  Part2 = FTDI Basic Programmer
  Part3 = Arduino Pro Mini v13

nets:
  N1: RFM1.3_MOSI, Part3.D12/MISO
  N2: RFM1.4_SCK, Part3.D13/SCK
  N3: RFM1.5_NSS_(CS), Part3.D11_PWM/MOSI
  N4: RFM1.6_RESET, Part3.D10_PWM/SS
  GND: RFM1.10_GND, Part2.CTS, Part2.GND, Part3.GND
  N5: RFM1.13_3.3V, Part3.RAW
  N6: RFM1.14_DIO0, Part3.D2
  N7: Part2.DTR, Part3.DTR
  N8: Part2.RXI, Part3.D0/TX
  N9: Part2.TXO, Part3.D1/RX
  N10: Part2.POWER, Part3.VCC

custom parts:
  RFM69HCW ISM Transciever: RF Transceiver by Hope RF. Well supported Arduino libraries are available. This ISM band transceiver is available in several frequencies e.g. 433MHz and 915MHz and it is also available in various feature versions.
