# Fritzing sketch rover_circuit_recovered (saved by Fritzing 0.9.2b)
breadboards: 1
perfboards: 1

parts:
  BeagleBone1 = BeagleBone Black
  GPS1 = Adafruit Ultimate GPS Breakout
  INA1 = INA219 DC Current Sensor Breakout  # not connected
  FRONTMOTORS = Motor Driver 1A Dual TB6612FNG  # not connected
  REARMOTORS = Motor Driver 1A Dual TB6612FNG  # not connected
  IMU1 = Adafruit 10-DOF IMU Breakout
  RFM1 = RFM69HCW ISM Transciever
  JP2 = Header 4 [package=1x04-1mm-ra]
  BBB_I2C = Header 4 [package=1x04-1mm-ra]  # not connected
  FRONTA = Header 2 [package=jst-2-pth-kit]
  FRONTB = Header 2 [package=jst-2-pth-kit]
  REARB = Header 2 [package=jst-2-pth-kit]
  REARA = Header 2 [package=jst-2-pth-kit]
  VM(7V) = Header 2 [package=jst-2-pth-kit]  # not connected
  REARA_2 = DC Motor
  REARB_2 = DC Motor
  FRONTB_2 = DC Motor
  FRONTA_2 = DC Motor
  10DOF = Header 4 [package=1x04-1mm-ra]
  BBB_SPI0 = Header 4 [package=1x04-1mm-ra]
  CURRENTSENSOR = Header 4 [package=1x04-1mm-ra]  # not connected
  BBB_I2C_2 = Header 4 [package=1x04-1mm-ra]  # not connected
  BBB_UART = Header 4 [package=1x04-1mm-ra]  # not connected

nets:
  GND: BeagleBone1.no_name_yet#6, BeagleBone1.no_name_yet#7, GPS1.GND, GPS1.VIN
  N1: BeagleBone1.no_name_yet#17, RFM1.5_NSS_(CS), JP2.4, BBB_SPI0.3
  N2: BeagleBone1.no_name_yet#18, RFM1.3_MOSI, JP2.2, BBB_SPI0.4
  N3: BeagleBone1.no_name_yet#21, RFM1.2_MISO, JP2.1, BBB_SPI0.2
  N4: BeagleBone1.no_name_yet#22, RFM1.4_SCK, JP2.3, BBB_SPI0.1
  N5: BeagleBone1.no_name_yet#23, BeagleBone1.no_name_yet#24, BeagleBone1.no_name_yet#202, GPS1.RX
  N6: BeagleBone1.no_name_yet#25, BeagleBone1.no_name_yet#26, BeagleBone1.no_name_yet#203, GPS1.TX
  N7: IMU1.3Vo, 10DOF.1
  N8: IMU1.GND, 10DOF.2
  N9: IMU1.SCL, IMU1.SDA, 10DOF.3
  N10: FRONTA.1, FRONTA_2.pin_1
  N11: FRONTA.2, FRONTA_2.pin_2
  N12: FRONTB.1, FRONTB_2.pin_1
  N13: FRONTB.2, FRONTB_2.pin_2
  N14: REARB.1, REARB_2.pin_1
  N15: REARB.2, REARB_2.pin_2
  N16: REARA.1, REARA_2.pin_1
  N17: REARA.2, REARA_2.pin_2

custom parts:
  BeagleBone Black: BeagleBone Black rev. A5B
  INA219 DC Current Sensor Breakout: INA DC Current Sensor Breakout
  RFM69HCW ISM Transciever: RF Transceiver by Hope RF. Well supported Arduino libraries are available. This ISM band transceiver is available in several frequencies e.g. 433MHz and 915MHz and it is also available in various feature versions.
