# Fritzing sketch subsystem_drive (saved by Fritzing 0.9.2b)

parts:
  M1 = DC Motor  # not connected
  M2 = DC Motor  # not connected
  Part1 = Motor Driver 1A Dual TB6612FNG  # not connected
  Part2 = Motor Driver 1A Dual TB6612FNG
  M3 = DC Motor
  M4 = DC Motor
  BeagleBone1 = BeagleBone Black  # not connected

nets:
  N1: Part2.B01, M3.pin_1
  N2: Part2.B02, M3.pin_2
  N3: Part2.A02, M4.pin_1
  N4: Part2.A01, M4.pin_2

custom parts:
  BeagleBone Black: BeagleBone Black rev. A5B
