# Fritzing sketch subsystem_power (saved by Fritzing 0.9.2b)

parts:
  CHARGER1 = USB_LiIon_LiPoly_Charger_v1.2
  INA1 = INA219 DC Current Sensor Breakout
  CHARGER2 = USB_LiIon_LiPoly_Charger_v1.2
  Solar_Panel_6V_(1) = solar_pannel
  Solar_Panel_(2) = solar_pannel
  DC/DC_converter = mystery part, 4 pins [chip_label="DC/DC converter"]
  U1 = LIPO-2000mAh [package=lipo-2000]
  U2 = LIPO-2000mAh [package=lipo-2000]

nets:
  N1: CHARGER1.batt_minus_1, U2.-
  N2: CHARGER1.batt_plus_1, U2.+
  N3: CHARGER1.dcin_minus_1, Solar_Panel_6V_(1).aún_sin_nombre#0
  N4: CHARGER1.dcin_plus_1, Solar_Panel_6V_(1).aún_sin_nombre#1
  N5: CHARGER1.load_minus_2, DC/DC_converter.pin4
  N6: CHARGER1.load_plus_2, CHARGER2.load_minus_2
  N7: INA1.Vin-2, CHARGER2.load_plus_2
  N8: INA1.Vin+2, DC/DC_converter.pin3
  N9: CHARGER2.batt_minus_1, U1.-
  N10: CHARGER2.batt_plus_1, U1.+
  N11: CHARGER2.dcin_minus_1, Solar_Panel_(2).aún_sin_nombre#0
  N12: CHARGER2.dcin_plus_1, Solar_Panel_(2).aún_sin_nombre#1

notes:
  input: 7.4V 2000mAh
  output: 4.8V XA
  outputs to microcontroller
  Current monitor requires 3-5V power from microcontroller
  7.4V unregulated to VM on motor drivers.

custom parts:
  INA219 DC Current Sensor Breakout: INA DC Current Sensor Breakout
  solar_pannel: Solar pannel
